# Fritzing sketch HC-SR04_GM009605_fritzing (saved by Fritzing 0.9.3b)
breadboards: 1

parts:
  Part1 = Arduino Uno (Rev3)
  Grove1 = Grove OLED 128x96
  hc-sr1 = hc-sr04

nets:
  N1: Part1.A3, Grove1.SDA
  N2: Part1.A4/SDA, Grove1.SCL
  N3: Part1.D11_PWM/MOSI, hc-sr1.Trig
  N4: Part1.D12/MISO, hc-sr1.Echo
  VCC: Part1.3V3, Grove1.VCC, hc-sr1.VCC
  GND: Part1.GND, Grove1.GND, hc-sr1.GND
